# Fritzing sketch Hardware Diagram (saved by Fritzing 0.9.10b)

parts:
  L298N1 = L298N DC motor driver  # not connected
  A1 = Teensy 4.1
  DC_Mot_Enc2 = DC Motor with two-phase encoder [part_number=VT-E-G25A-06-177E]  # not connected
  Part1 = InvenSense MPU6050
  L298N2 = L298N DC motor driver  # not connected
  DC_Mot_Enc3 = DC Motor with two-phase encoder [part_number=VT-E-G25A-06-177E]  # not connected
  DC_Mot_Enc4 = DC Motor with two-phase encoder [part_number=VT-E-G25A-06-177E]  # not connected
  DC_Mot_Enc5 = DC Motor with two-phase encoder [part_number=VT-E-G25A-06-177E]
  J1 = Basic Servo  # not connected
  J2 = Basic Servo  # not connected
  Part3 = I2C level shifter bidirectional  # not connected
  J3 = Power Jack [package=power_jack_pth_lock]
  J4 = Power Jack [package=power_jack_pth_lock]  # not connected
  J5 = Power Jack [package=power_jack_pth_lock]

nets:
  N1: A1.Pin_18, Part1.SDA
  N2: A1.Pin_19, Part1.SCL
  N3: A1.Pin_62, DC_Mot_Enc5.Quad_Encoder_+5V
  N4: A1.Pin_63, DC_Mot_Enc5.Quad_Encoder_Ground
  GND: J3.GND, J5.GND

notes:
  STERO CAMERA PINS
  SDA
  SCL<module fritzingVersion="0.9.10b.2022-07-01.CD-2134-0-40d23c29">
  <boundingRects>
  <boundingRect rect="400.483 -250.526 26.717 57.0435" name="Breadboard View"/>
  <boundingRect rect="0 0 0 0" name="PCB View"/>
  <boundingRect rect="0 0 0 0" name="Schematic View"/>
  </boundingRects>
  <instances>
  <instance path=":/resources/parts/core/wire.fzp" moduleIdRef="WireModuleID" modelIndex="85524199">
  <title>Wire19</title>
  <views>
  <breadboardView layer="breadboardWire">
  <geometry x2="-17.6829" x1="0" y2="48.0095" z="3.50004" y1="0" y="-246.009" wireFlags="64" x="422.683"/>
  <wireExtras banded="0" opacity="1" mils="22.2222" color="#404040"/>
  <connectors>
  <connector layer="breadboardWire" connectorId="connector1">
  <geometry y="0" x="0"/>
  <connects/>
  </connector>
  </connectors>
  </breadboardView>
  <schematicView layer="schematicTrace">
  <geometry x2="-20.6675" x1="0" y2="43.335" z="5.50006" y1="0" y="-242.009" wireFlags="64" x="427.016"/>
  <wireExtras banded="0" opacity="1" mils="9.7222" color="#404040"/>
  <connectors>
  <connector layer="schematicTrace" connectorId="connector1">
  <geometry y="0" x="0"/>
  <connects/>
  </connector>
  </connectors>
  </schematicView>
  <pcbView layer="copper1trace">
  <geometry x2="-20.6675" x1="0" y2="43.335" z="9.50006" y1="0" y="-242.009" wireFlags="64" x="427.016"/>
  <wireExtras banded="0" opacity="1" mils="11.1111" color="#f2c600"/>
  <connectors>
  <connector layer="copper1trace" connectorId="connector1">
  <geometry y="0" x="0"/>
  <connects/>
  </connector>
  </connectors>
  </pcbView>
  </views>
  </instance>
  </instances>
  </module>
  INT
  FSYNC
  JETSON XAVIER EVEN PINS
  JETSON XAVIER ODD PINS
  Wire colors are different here.
  Blue should be Yellow (as is on our robot)
  Green should be White
  Yellow should be Orange (VERIFY)
  White should be Green (VERIFY)
  LEFT, 12V Power
  MIDDLE, 5V Power
  RIGHT, 3V3 Power

custom parts:
  L298N DC motor driver: 2x DC motor driver with 78M05 positive voltage regulator (7..35 V) L298N: max 46 V, 2 A Set 5 V Enable jumper to enable 5 V regultor (needed for the L298N) and +5 V output at screw terminal or supply external +5 V at screw terminal Set ENA and/or ENB to +5 V to enable motor permanently or supply ENA and/or ENB with PWM signal IN1 and IN2 set rotation directory for motor A (OUT1/OUT2) IN2 and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
  Teensy 4.1: The Teensy is a complete USB-based microcontoller development system, in a very small footprint, capable of implementing many types of projects. All programming is done via the USB port. No special programmer is needed, only a standard micro-USB cable and a PC or Macintosh with a USB port.
